// Logisim project 1-flip_flop_D_e_JK.circ as structural Verilog: 2 circuits, main circuit Flip_Flop_jk
module Flip_Flop_jk (
  input  Preset,
  input  J,
  input  Clock,
  input  k,
  input  Clear,
  output Q,
  output Q_barr
);

  wire nand_1_out, nand_2_out, nand_3_out, nand_4_out, nand_5_out, nand_6_out, not_1_out;

  Clock u_Clock ();  // open: out
  not not_1 (not_1_out, Clock);
  nand nand_1 (nand_1_out, Q_barr, J, not_1_out);
  nand nand_2 (nand_2_out, not_1_out, k, Q);
  nand nand_3 (nand_3_out, Preset, nand_1_out, nand_4_out);
  nand nand_4 (nand_4_out, nand_3_out, nand_2_out, Clear);
  nand nand_5 (nand_5_out, nand_3_out, Clock);
  nand nand_6 (nand_6_out, Clock, nand_4_out);
  nand nand_7 (Q, Preset, nand_5_out, Q_barr);
  nand nand_8 (Q_barr, Q, nand_6_out, Clear);

  // Notes on the sheet:
  //   X
  //   Y
  //   Flip-Flop JK Master Slave com Preset e Clear
  //   Clock
endmodule

module Flip_Flop_d (
  input  in_1,
  input  D,
  input  Clock,
  input  in_4,
  output out_5,
  output out_6
);

  wire not_1_out;

  not not_1 (not_1_out, D);
  Flip_Flop_jk flip_flop_jk_1 (
    .J(D), .Clock(Clock), .k(not_1_out), .Q(out_5), .Q_barr(out_6), .Preset(in_1), .Clear(in_4));
endmodule
