// Logisim project 10-ULA.circ as structural Verilog: 6 circuits, main circuit main
module main (
  input  [7:0] Entrada_A,
  input  [7:0] Entrada_B,
  input  in_3,
  input  in_4,
  input  in_5,
  input  in_6,
  input  [2:0] in_7,
  input  in_8,
  input  in_9,
  input  in_10,
  input  in_11,
  output [7:0] out_12
);

  wire [7:0] and_1_out, \deslocador_left_1_saída , \deslocador_rigth_1_saída , multiplexador_8bits_1_out_4,
       \multplex8x1_1_x_saída , \multplex8x1_2_x_saída , nand_1_out, nor_1_out, not_1_out, not_2_out,
       or_1_out, somador_8bits_1_out_5, \sub_8bits_1_saída , xor_1_out;

  multiplexador_8bits multiplexador_8bits_1 (
    .in_1(Entrada_A), .in_2(Entrada_B), .in_3(in_5), .out_4(multiplexador_8bits_1_out_4));
  assign and_1_out = Entrada_A & Entrada_B;  // AND_Gate and_1, 8 bits wide
  assign or_1_out = Entrada_A | Entrada_B;  // OR_Gate or_1, 8 bits wide
  assign not_1_out = ~Entrada_A;  // NOT_Gate not_1, 8 bits wide
  assign not_2_out = ~Entrada_B;  // NOT_Gate not_2, 8 bits wide
  assign nand_1_out = ~(Entrada_A & Entrada_B);  // NAND_Gate nand_1, 8 bits wide
  assign nor_1_out = ~(Entrada_A | Entrada_B);  // NOR_Gate nor_1, 8 bits wide
  assign xor_1_out = Entrada_A ^ Entrada_B;  // XOR_Gate xor_1, 8 bits wide
  Deslocador_left deslocador_left_1 (
    .Entrada(multiplexador_8bits_1_out_4), .\Saída (\deslocador_left_1_saída ), .Deslocador(in_3));
  deslocador_rigth deslocador_rigth_1 (
    .ENTRADA(multiplexador_8bits_1_out_4), .\Saída (\deslocador_rigth_1_saída ), .deslocador(in_4));
  sub_8bits sub_8bits_1 (
    .Entrada_A(Entrada_A), .Borrow_in(in_9), .Entrada_B(Entrada_B), .Borrow_out(in_8),
    .\Saída (\sub_8bits_1_saída ));
  Somador_8bits somador_8bits_1 (
    .Carry_in(in_11), .Carry_out(in_10), .out_5(somador_8bits_1_out_5), .in_1(Entrada_B), .in_2(Entrada_A));
  Multplex8x1 multplex8x1_1 (
    .A0(and_1_out), .A1(or_1_out), .A2(not_1_out), .A3(not_2_out), .A4(nand_1_out), .A5(nor_1_out),
    .A6(xor_1_out), .A7(\deslocador_left_1_saída ), .Selecionador(in_7), .\X_saída (\multplex8x1_1_x_saída ));
  Multplex8x1 multplex8x1_2 (
    .A0(\deslocador_rigth_1_saída ), .A1(\sub_8bits_1_saída ), .A2(somador_8bits_1_out_5),
    .Selecionador(in_7), .\X_saída (\multplex8x1_2_x_saída ));  // open: A3, A4, A5, A6, A7
  multiplexador_8bits multiplexador_8bits_2 (
    .in_1(\multplex8x1_1_x_saída ), .in_2(\multplex8x1_2_x_saída ), .in_3(in_6), .out_4(out_12));
endmodule

module sub_complet (
  input  A,
  input  B,
  input  Borrow_in,
  output Diff,
  output Borrow_out
);

  wire and_1_out, and_2_out, and_3_out, not_1_out, not_2_out, xor_1_out;

  not not_1 (not_1_out, A);
  not not_2 (not_2_out, A);
  xor xor_1 (xor_1_out, A, B);
  and and_1 (and_1_out, B, Borrow_in);
  and and_2 (and_2_out, not_1_out, Borrow_in);
  and and_3 (and_3_out, not_2_out, B);
  xor xor_2 (Diff, xor_1_out, Borrow_in);
  or or_1 (Borrow_out, and_1_out, and_2_out, and_3_out);
endmodule

module sub_8bits (
  input  [7:0] Entrada_A,
  input  Borrow_out,
  input  Borrow_in,
  input  [7:0] Entrada_B,
  output [7:0] \Saída 
);

  wire sub_complet_2_borrow_out, sub_complet_3_borrow_out, sub_complet_4_borrow_out,
       sub_complet_5_borrow_out, sub_complet_6_borrow_out, sub_complet_7_borrow_out, sub_complet_8_borrow_out;

  sub_complet sub_complet_1 (
    .A(Entrada_A[7]), .B(Entrada_B[7]), .Borrow_in(sub_complet_2_borrow_out), .Diff(\Saída [7]),
    .Borrow_out(Borrow_in));
  sub_complet sub_complet_2 (
    .A(Entrada_A[6]), .B(Entrada_B[6]), .Borrow_in(sub_complet_3_borrow_out), .Diff(\Saída [6]),
    .Borrow_out(sub_complet_2_borrow_out));
  sub_complet sub_complet_3 (
    .A(Entrada_A[5]), .B(Entrada_B[5]), .Borrow_in(sub_complet_4_borrow_out), .Diff(\Saída [5]),
    .Borrow_out(sub_complet_3_borrow_out));
  sub_complet sub_complet_4 (
    .A(Entrada_A[4]), .B(Entrada_B[4]), .Borrow_in(sub_complet_5_borrow_out), .Diff(\Saída [4]),
    .Borrow_out(sub_complet_4_borrow_out));
  sub_complet sub_complet_5 (
    .A(Entrada_A[3]), .B(Entrada_B[3]), .Borrow_in(sub_complet_6_borrow_out), .Diff(\Saída [3]),
    .Borrow_out(sub_complet_5_borrow_out));
  sub_complet sub_complet_6 (
    .A(Entrada_A[2]), .B(Entrada_B[2]), .Borrow_in(sub_complet_7_borrow_out), .Diff(\Saída [2]),
    .Borrow_out(sub_complet_6_borrow_out));
  sub_complet sub_complet_7 (
    .A(Entrada_A[1]), .B(Entrada_B[1]), .Borrow_in(sub_complet_8_borrow_out), .Diff(\Saída [1]),
    .Borrow_out(sub_complet_7_borrow_out));
  sub_complet sub_complet_8 (
    .A(Entrada_A[0]), .B(Entrada_B[0]), .Borrow_in(Borrow_out), .Diff(\Saída [0]),
    .Borrow_out(sub_complet_8_borrow_out));
endmodule

module Deslocador_left (
  input  [7:0] Entrada,
  input  Deslocador,
  output [7:0] \Saída 
);

  Multiplexer multiplexer_1 (.in0(Entrada[7]), .in1(Entrada[6]), .out(\Saída [7]), .sel(Deslocador));  // open: en
  Multiplexer multiplexer_2 (.in0(Entrada[6]), .in1(Entrada[5]), .out(\Saída [6]), .sel(Deslocador));  // open: en
  Multiplexer multiplexer_3 (.in0(Entrada[5]), .in1(Entrada[4]), .out(\Saída [5]), .sel(Deslocador));  // open: en
  Multiplexer multiplexer_4 (.in0(Entrada[4]), .in1(Entrada[3]), .out(\Saída [4]), .sel(Deslocador));  // open: en
  Multiplexer multiplexer_5 (.in0(Entrada[3]), .in1(Entrada[2]), .out(\Saída [3]), .sel(Deslocador));  // open: en
  Multiplexer multiplexer_6 (.in0(Entrada[2]), .in1(Entrada[1]), .out(\Saída [2]), .sel(Deslocador));  // open: en
  Multiplexer multiplexer_7 (.in0(Entrada[1]), .in1(Entrada[0]), .out(\Saída [1]), .sel(Deslocador));  // open: en
  Multiplexer multiplexer_8 (.in0(Entrada[0]), .in1(1'b0), .out(\Saída [0]), .sel(Deslocador));  // open: en
endmodule

module deslocador_rigth (
  input  deslocador,
  input  [7:0] ENTRADA,
  output [7:0] \Saída 
);

  Multiplexer multiplexer_1 (.in0(ENTRADA[7]), .in1(1'b0), .out(\Saída [7]), .sel(deslocador));  // open: en
  Multiplexer multiplexer_2 (.in0(ENTRADA[6]), .in1(ENTRADA[7]), .out(\Saída [6]), .sel(deslocador));  // open: en
  Multiplexer multiplexer_3 (.in0(ENTRADA[5]), .in1(ENTRADA[6]), .out(\Saída [5]), .sel(deslocador));  // open: en
  Multiplexer multiplexer_4 (.in0(ENTRADA[4]), .in1(ENTRADA[5]), .out(\Saída [4]), .sel(deslocador));  // open: en
  Multiplexer multiplexer_5 (.in0(ENTRADA[3]), .in1(ENTRADA[4]), .out(\Saída [3]), .sel(deslocador));  // open: en
  Multiplexer multiplexer_6 (.in0(ENTRADA[2]), .in1(ENTRADA[3]), .out(\Saída [2]), .sel(deslocador));  // open: en
  Multiplexer multiplexer_7 (.in0(ENTRADA[1]), .in1(ENTRADA[2]), .out(\Saída [1]), .sel(deslocador));  // open: en
  Multiplexer multiplexer_8 (.in0(ENTRADA[0]), .in1(ENTRADA[1]), .out(\Saída [0]), .sel(deslocador));  // open: en
endmodule

module multplex16x1 (
  input  [7:0] in_1,
  input  [7:0] in_2,
  input  [7:0] in_3,
  input  [7:0] in_4,
  input  [7:0] in_5,
  input  [7:0] in_6,
  input  [7:0] in_7,
  input  [7:0] in_8,
  input  [7:0] in_9,
  input  [7:0] in_10,
  input  [7:0] in_11,
  input  [7:0] in_12,
  input  [7:0] in_13,
  input  [7:0] in_14,
  input  [7:0] in_15,
  input  [7:0] in_16,
  input  [3:0] in_17,
  output [7:0] out_18
);

  wire [7:0] \multplex8x1_1_x_saída , undriven;

  Multplex8x1 multplex8x1_1 (
    .A0(in_1), .A1(in_2), .A2(in_3), .A3(in_4), .A4(in_5), .A5(in_6), .A6(in_7), .A7(in_8),
    .Selecionador(in_17[2:0]), .\X_saída (\multplex8x1_1_x_saída ));
  Multplex8x1 multplex8x1_2 (
    .A0(in_9), .A1(in_10), .A2(in_11), .A3(in_12), .A4(in_13), .A5(in_14), .A6(in_15), .A7(in_16),
    .Selecionador(in_17[2:0]));  // open: X_saída
  multiplexador_8bits multiplexador_8bits_1 (
    .in_1(\multplex8x1_1_x_saída ), .in_2(undriven), .in_3(in_17[3]), .out_4(out_18));
endmodule
