// Logisim project 16-Decodificador de 7 Segmentos Projete um circuito que converta um número binário.circ as structural Verilog: 2 circuits, main circuit main
module main (
  input  A3,
  input  A2,
  input  A1,
  input  A0,
  output out_5,
  output out_6,
  output out_7,
  output out_8,
  output out_9,
  output out_10,
  output out_11
);

  wire and_1_out, and_2_out, and_3_out, and_4_out, and_5_out, and_6_out, and_7_out, and_8_out, and_9_out,
       and_10_out, not_1_out, not_2_out, not_3_out, xnor_1_out, xnor_2_out, xor_1_out;

  and and_1 (and_1_out, not_3_out, A1);
  xor xor_1 (xor_1_out, A1, A2);
  or or_1 (out_5, and_1_out, xor_1_out, A3);
  and and_2 (and_2_out, not_3_out, A2);
  and and_3 (and_3_out, not_2_out, A2);
  and and_4 (and_4_out, not_3_out, not_2_out);
  or or_2 (out_6, and_2_out, and_3_out, and_4_out, A3);
  and and_5 (and_5_out, not_3_out, A1);
  or or_3 (out_7, and_5_out, and_6_out);
  and and_6 (and_6_out, not_3_out, not_1_out);
  and and_7 (and_7_out, A0, not_2_out, A2);
  _7_Segment_Display u_7_segment_display_1 (
    .g(out_5), .f(out_6), .a(out_11), .b(out_10), .e(out_7), .d(out_8), .c(out_9));  // open: dp
  and and_8 (and_8_out, not_3_out, A1);
  and and_9 (and_9_out, A1, not_1_out);
  or or_4 (out_8, and_7_out, and_8_out, A3, and_9_out, and_10_out);
  and and_10 (and_10_out, not_3_out, not_1_out);
  or or_5 (out_9, A0, not_2_out, A2);
  xnor xnor_1 (xnor_1_out, A0, A1);
  or or_6 (out_10, xnor_1_out, not_1_out);
  or or_7 (out_11, A1, A3, xnor_2_out);
  not not_1 (not_1_out, A2);
  not not_2 (not_2_out, A1);
  not not_3 (not_3_out, A0);
  xnor xnor_2 (xnor_2_out, A0, A2);
endmodule

module Decodificador (
  input  [3:0] in_1
);

  wire main_1_out_5, main_1_out_6, main_1_out_7, main_1_out_8, main_1_out_9, main_1_out_10, main_1_out_11;

  main main_1 (
    .out_5(main_1_out_5), .out_6(main_1_out_6), .out_7(main_1_out_7), .out_8(main_1_out_8),
    .out_9(main_1_out_9), .out_10(main_1_out_10), .out_11(main_1_out_11), .A3(in_1[3]), .A2(in_1[2]),
    .A1(in_1[1]), .A0(in_1[0]));
  _7_Segment_Display u_7_segment_display_1 (
    .g(main_1_out_5), .f(main_1_out_6), .a(main_1_out_11), .b(main_1_out_10), .e(main_1_out_7),
    .d(main_1_out_8), .c(main_1_out_9));  // open: dp
endmodule
