// Logisim project 2-Multiplexador_4entradas.circ as structural Verilog: 1 circuit, main circuit multiplex4
module multiplex4 (
  input  S1,
  input  S2,
  input  I0,
  input  I1,
  input  I2,
  input  I3,
  output X
);

  wire and_1_out, and_2_out, and_3_out, and_4_out, not_1_out, not_2_out, not_3_out, not_4_out;

  not not_1 (not_1_out, S2);
  not not_2 (not_2_out, S1);
  not not_3 (not_3_out, S1);
  not not_4 (not_4_out, S2);
  and and_1 (and_1_out, I0, not_1_out, not_2_out);
  and and_2 (and_2_out, I1, S2, not_3_out);
  and and_3 (and_3_out, I2, not_4_out, S1);
  and and_4 (and_4_out, I3, S2, S1);
  or or_1 (X, and_1_out, and_2_out, and_3_out, and_4_out);

  // Notes on the sheet:
  //   Multiplexador de 4 entradas e dois seletores
endmodule
