// Logisim project 3-PortaXor_with_and_or_not.circ as structural Verilog: 1 circuit, main circuit Xor
module Xor (
  input  A,
  input  B,
  output S
);

  wire and_1_out, and_2_out, not_1_out, not_2_out;

  not not_1 (not_1_out, B);
  not not_2 (not_2_out, A);
  and and_1 (and_1_out, A, not_1_out);
  and and_2 (and_2_out, not_2_out, B);
  or or_1 (S, and_1_out, and_2_out);

  // Notes on the sheet:
  //   Porta lógica xor utilizando portas and, or e not
endmodule
