// Logisim project 4-8-Somador8bits_e_soma_inteiro4.circ as structural Verilog: 5 circuits, main circuit xor
module \xor  (
  input  A,
  input  B,
  output X
);

  wire and_1_out, and_2_out, not_1_out, not_2_out;

  not not_1 (not_1_out, B);
  not not_2 (not_2_out, A);
  and and_1 (and_1_out, A, not_1_out);
  and and_2 (and_2_out, not_2_out, B);
  or or_1 (X, and_1_out, and_2_out);
endmodule

module Somador_completo (
  input  A,
  input  B,
  input  Carry_in,
  output Carry_out,
  output S
);

  wire and_1_out, and_2_out, xor_1_x;

  and and_1 (and_1_out, A, B);
  \xor  xor_1 (.A(A), .B(B), .X(xor_1_x));
  and and_2 (and_2_out, xor_1_x, Carry_in);
  or or_1 (Carry_out, and_1_out, and_2_out);
  \xor  xor_2 (.A(xor_1_x), .B(Carry_in), .X(S));
endmodule

module Somador_4bits (
  input  A3,
  input  B3,
  input  A2,
  input  B2,
  input  A1,
  input  B1,
  input  A0,
  input  B0,
  input  Carry_in,
  output Carry_out,
  output S3,
  output S2,
  output S1,
  output S0
);

  wire somador_completo_2_carry_out, somador_completo_3_carry_out, somador_completo_4_carry_out;

  Somador_completo somador_completo_1 (
    .A(A3), .B(B3), .Carry_out(Carry_out), .Carry_in(somador_completo_2_carry_out), .S(S3));
  Somador_completo somador_completo_2 (
    .A(A2), .B(B2), .Carry_out(somador_completo_2_carry_out), .Carry_in(somador_completo_3_carry_out), .S(S2));
  Somador_completo somador_completo_3 (
    .A(A1), .B(B1), .Carry_out(somador_completo_3_carry_out), .Carry_in(somador_completo_4_carry_out), .S(S1));
  Somador_completo somador_completo_4 (
    .A(A0), .B(B0), .Carry_out(somador_completo_4_carry_out), .Carry_in(Carry_in), .S(S0));
endmodule

module Somador_8bits (
  input  [7:0] in_1,
  input  [7:0] in_2,
  input  Carry_in,
  output Carry_out,
  output [7:0] out_5
);

  wire somador_4bits_2_carry_out;

  Somador_4bits somador_4bits_1 (
    .A0(in_1[4]), .B0(in_2[4]), .A1(in_1[5]), .B1(in_2[5]), .A2(in_1[6]), .B2(in_2[6]), .A3(in_1[7]),
    .B3(in_2[7]), .S0(out_5[4]), .S1(out_5[5]), .S2(out_5[6]), .S3(out_5[7]), .Carry_out(Carry_out),
    .Carry_in(somador_4bits_2_carry_out));
  Somador_4bits somador_4bits_2 (
    .A0(in_1[0]), .B0(in_2[0]), .A1(in_1[1]), .B1(in_2[1]), .A2(in_1[2]), .B2(in_2[2]), .A3(in_1[3]),
    .B3(in_2[3]), .S0(out_5[0]), .S1(out_5[1]), .S2(out_5[2]), .S3(out_5[3]),
    .Carry_out(somador_4bits_2_carry_out), .Carry_in(Carry_in));
endmodule

module somador8bits_4 (
  input  in_1,
  input  [7:0] Entrada,
  input  in_3,
  output [7:0] Saida
);

  Somador_8bits somador_8bits_1 (.Carry_in(in_3), .Carry_out(in_1), .out_5(Saida), .in_1(Entrada), .in_2(8'h4));

  // Notes on the sheet:
  //   Valor 4 em binário
endmodule
