// Logisim project 5-Memoria Rom de 8 bits.circ as structural Verilog: 1 circuit, main circuit main
module main (
  input  A2,
  input  A1,
  input  A0,
  output [7:0] out_4
);

  wire _0_out, _1_out, _2_out, _3_out, _4_out, _5_out, _6_out, _7_out, not_1_out, not_2_out, not_3_out;

  not not_1 (not_1_out, A2);
  not not_2 (not_2_out, A1);
  not not_3 (not_3_out, A0);
  or or_1 (out_4[0], _1_out, _3_out, _5_out, _6_out);
  and _0 (_0_out, not_1_out, not_2_out, not_3_out);
  and _1 (_1_out, not_1_out, not_2_out, A0);
  and _2 (_2_out, not_1_out, A1, not_3_out);
  and _3 (_3_out, not_1_out, A1, A0);
  and _4 (_4_out, A2, not_2_out, not_3_out);
  and _5 (_5_out, A2, not_2_out, A0);
  and _6 (_6_out, A2, A1, not_3_out);
  and _7 (_7_out, A2, A1, A0);
  or or_2 (out_4[1], _0_out, _3_out, _5_out, _7_out);
  or or_3 (out_4[2], _1_out, _2_out, _5_out, _7_out);
  or or_4 (out_4[3], _0_out, _2_out, _5_out, _6_out);
  or or_5 (out_4[4], _1_out, _3_out, _4_out, _6_out);
  or or_6 (out_4[5], _0_out, _3_out, _4_out, _7_out);
  or or_7 (out_4[6], _1_out, _2_out, _4_out, _7_out);
  or or_8 (out_4[7], _0_out, _2_out, _4_out, _6_out);

  // Notes on the sheet:
  //   A2: pull=up
  //   A0: pull=up
  //   A1: pull=up
  //   Memoria rom que armazena  sequência toggle alternada
endmodule
