// Logisim project 6-Memoria_Ram_8bits.circ as structural Verilog: 6 circuits, main circuit registrador_8bits
module registrador_8bits (
  input  Clock,
  input  Preset,
  input  Clear,
  input  [7:0] in_4,
  output [7:0] Saida
);

  Flip_Flop_d flip_flop_d_1 (.D(in_4[7]), .Clock(Clock), .out_5(Saida[7]), .in_1(Preset), .in_4(Clear));  // open: out_6
  Flip_Flop_d flip_flop_d_2 (.D(in_4[6]), .Clock(Clock), .out_5(Saida[6]), .in_1(Preset), .in_4(Clear));  // open: out_6
  Flip_Flop_d flip_flop_d_3 (.D(in_4[5]), .Clock(Clock), .out_5(Saida[5]), .in_1(Preset), .in_4(Clear));  // open: out_6
  Flip_Flop_d flip_flop_d_4 (.D(in_4[4]), .Clock(Clock), .out_5(Saida[4]), .in_1(Preset), .in_4(Clear));  // open: out_6
  Flip_Flop_d flip_flop_d_5 (.D(in_4[3]), .Clock(Clock), .out_5(Saida[3]), .in_1(Preset), .in_4(Clear));  // open: out_6
  Flip_Flop_d flip_flop_d_6 (.D(in_4[2]), .Clock(Clock), .out_5(Saida[2]), .in_1(Preset), .in_4(Clear));  // open: out_6
  Flip_Flop_d flip_flop_d_7 (.D(in_4[1]), .Clock(Clock), .out_5(Saida[1]), .in_1(Preset), .in_4(Clear));  // open: out_6
  Flip_Flop_d flip_flop_d_8 (.D(in_4[0]), .Clock(Clock), .out_5(Saida[0]), .in_1(Preset), .in_4(Clear));  // open: out_6
endmodule

module multiplexador_8bits (
  input  [7:0] in_1,
  input  [7:0] in_2,
  input  in_3,
  output [7:0] out_4
);

  multiplex_4x1 multiplex_4x1_1 (.B(in_2[3:0]), .A(in_1[3:0]), .in_1(in_3), .out_4(out_4[3:0]));
  multiplex_4x1 multiplex_4x1_2 (.B(in_2[7:4]), .A(in_1[7:4]), .in_1(in_3), .out_4(out_4[7:4]));
endmodule

module multiplex_4x1 (
  input  in_1,
  input  [3:0] B,
  input  [3:0] A,
  output [3:0] out_4
);

  wire and_1_out, and_2_out, and_3_out, and_4_out, and_5_out, and_6_out, and_7_out, and_8_out, not_1_out,
       not_2_out, not_3_out, not_4_out;

  not not_1 (not_1_out, in_1);
  not not_2 (not_2_out, in_1);
  not not_3 (not_3_out, in_1);
  not not_4 (not_4_out, in_1);
  and and_1 (and_1_out, A[0], not_1_out);
  and and_2 (and_2_out, B[0], in_1);
  and and_3 (and_3_out, A[1], not_2_out);
  and and_4 (and_4_out, B[1], in_1);
  and and_5 (and_5_out, A[2], not_3_out);
  and and_6 (and_6_out, B[2], in_1);
  and and_7 (and_7_out, A[3], not_4_out);
  and and_8 (and_8_out, B[3], in_1);
  or or_1 (out_4[0], and_1_out, and_2_out);
  or or_2 (out_4[1], and_3_out, and_4_out);
  or or_3 (out_4[2], and_5_out, and_6_out);
  or or_4 (out_4[3], and_7_out, and_8_out);
endmodule

module Multplex8x1 (
  input  [7:0] A0,
  input  [7:0] A1,
  input  [7:0] A2,
  input  [7:0] A3,
  input  [7:0] A4,
  input  [7:0] A5,
  input  [7:0] A6,
  input  [7:0] A7,
  input  [2:0] Selecionador,
  output [7:0] \X_saída 
);

  wire [7:0] multiplexador_8bits_1_out_4, multiplexador_8bits_2_out_4, multiplexador_8bits_3_out_4,
       multiplexador_8bits_4_out_4, multiplexador_8bits_5_out_4, multiplexador_8bits_6_out_4;

  multiplexador_8bits multiplexador_8bits_1 (
    .in_1(A0), .in_2(A1), .in_3(Selecionador[0]), .out_4(multiplexador_8bits_1_out_4));
  multiplexador_8bits multiplexador_8bits_2 (
    .in_1(A2), .in_2(A3), .in_3(Selecionador[0]), .out_4(multiplexador_8bits_2_out_4));
  multiplexador_8bits multiplexador_8bits_3 (
    .in_1(A4), .in_2(A5), .in_3(Selecionador[0]), .out_4(multiplexador_8bits_3_out_4));
  multiplexador_8bits multiplexador_8bits_4 (
    .in_1(A6), .in_2(A7), .in_3(Selecionador[0]), .out_4(multiplexador_8bits_4_out_4));
  multiplexador_8bits multiplexador_8bits_5 (
    .in_1(multiplexador_8bits_1_out_4), .in_2(multiplexador_8bits_2_out_4), .in_3(Selecionador[1]),
    .out_4(multiplexador_8bits_5_out_4));
  multiplexador_8bits multiplexador_8bits_6 (
    .in_1(multiplexador_8bits_3_out_4), .in_2(multiplexador_8bits_4_out_4), .in_3(Selecionador[1]),
    .out_4(multiplexador_8bits_6_out_4));
  multiplexador_8bits multiplexador_8bits_7 (
    .in_1(multiplexador_8bits_5_out_4), .in_2(multiplexador_8bits_6_out_4), .in_3(Selecionador[2]),
    .out_4(\X_saída ));

  // Notes on the sheet:
  //   ENTRADAS
endmodule

module Ram_principal (
  input  [7:0] Entrada_D,
  input  Preset,
  input  Clear,
  input  W,
  input  [2:0] Seleciona_palavra,
  input  R,
  output [7:0] \Saída_x 
);

  wire and_1_out, and_2_out, and_3_out, and_4_out, and_5_out, and_6_out, and_7_out, and_8_out, and_9_out,
       and_10_out, and_11_out, and_12_out, and_13_out, and_14_out, and_15_out, and_16_out, not_1_out,
       not_2_out, not_3_out, not_4_out, not_5_out, not_6_out, not_7_out, not_8_out, not_9_out, not_10_out,
       not_11_out, not_12_out;
  wire [7:0] \multplex8x1_1_x_saída , registrador_8bits_1_saida, registrador_8bits_2_saida,
       registrador_8bits_3_saida, registrador_8bits_4_saida, registrador_8bits_5_saida,
       registrador_8bits_6_saida, registrador_8bits_7_saida, registrador_8bits_8_saida;

  not not_1 (not_1_out, Seleciona_palavra[0]);
  not not_2 (not_2_out, Seleciona_palavra[1]);
  not not_3 (not_3_out, Seleciona_palavra[2]);
  not not_4 (not_4_out, Seleciona_palavra[1]);
  not not_5 (not_5_out, Seleciona_palavra[2]);
  not not_6 (not_6_out, Seleciona_palavra[0]);
  not not_7 (not_7_out, Seleciona_palavra[2]);
  not not_8 (not_8_out, Seleciona_palavra[2]);
  not not_9 (not_9_out, Seleciona_palavra[0]);
  not not_10 (not_10_out, Seleciona_palavra[1]);
  not not_11 (not_11_out, Seleciona_palavra[1]);
  not not_12 (not_12_out, Seleciona_palavra[0]);
  and and_1 (and_1_out, not_1_out, not_2_out, not_3_out);
  and and_2 (and_2_out, Seleciona_palavra[0], not_4_out, not_5_out);
  and and_3 (and_3_out, not_6_out, Seleciona_palavra[1], not_7_out);
  and and_4 (and_4_out, Seleciona_palavra[0], Seleciona_palavra[1], not_8_out);
  and and_5 (and_5_out, not_9_out, not_10_out, Seleciona_palavra[2]);
  and and_6 (and_6_out, Seleciona_palavra[0], not_11_out, Seleciona_palavra[2]);
  and and_7 (and_7_out, not_12_out, Seleciona_palavra[1], Seleciona_palavra[2]);
  and and_8 (and_8_out, Seleciona_palavra[0], Seleciona_palavra[1], Seleciona_palavra[2]);
  and and_9 (and_9_out, and_1_out, W);
  and and_10 (and_10_out, and_2_out, W);
  and and_11 (and_11_out, and_3_out, W);
  and and_12 (and_12_out, and_4_out, W);
  and and_13 (and_13_out, and_5_out, W);
  and and_14 (and_14_out, and_6_out, W);
  and and_15 (and_15_out, and_7_out, W);
  and and_16 (and_16_out, and_8_out, W);
  registrador_8bits registrador_8bits_1 (
    .Clock(and_9_out), .Preset(Preset), .Clear(Clear), .Saida(registrador_8bits_1_saida), .in_4(Entrada_D));
  registrador_8bits registrador_8bits_2 (
    .Clock(and_10_out), .Preset(Preset), .Clear(Clear), .Saida(registrador_8bits_2_saida), .in_4(Entrada_D));
  registrador_8bits registrador_8bits_3 (
    .Clock(and_11_out), .Preset(Preset), .Clear(Clear), .Saida(registrador_8bits_3_saida), .in_4(Entrada_D));
  registrador_8bits registrador_8bits_4 (
    .Clock(and_12_out), .Preset(Preset), .Clear(Clear), .Saida(registrador_8bits_4_saida), .in_4(Entrada_D));
  registrador_8bits registrador_8bits_5 (
    .Clock(and_13_out), .Preset(Preset), .Clear(Clear), .Saida(registrador_8bits_5_saida), .in_4(Entrada_D));
  registrador_8bits registrador_8bits_6 (
    .Clock(and_14_out), .Preset(Preset), .Clear(Clear), .Saida(registrador_8bits_6_saida), .in_4(Entrada_D));
  registrador_8bits registrador_8bits_7 (
    .Clock(and_15_out), .Preset(Preset), .Clear(Clear), .Saida(registrador_8bits_7_saida), .in_4(Entrada_D));
  registrador_8bits registrador_8bits_8 (
    .Clock(and_16_out), .Preset(Preset), .Clear(Clear), .Saida(registrador_8bits_8_saida), .in_4(Entrada_D));
  Multplex8x1 multplex8x1_1 (
    .A0(registrador_8bits_1_saida), .A1(registrador_8bits_2_saida), .A2(registrador_8bits_3_saida),
    .A3(registrador_8bits_4_saida), .A4(registrador_8bits_5_saida), .A5(registrador_8bits_6_saida),
    .A6(registrador_8bits_7_saida), .A7(registrador_8bits_8_saida), .Selecionador(Seleciona_palavra),
    .\X_saída (\multplex8x1_1_x_saída ));
  assign \Saída_x  = R ? \multplex8x1_1_x_saída  : 8'bz;  // Controlled_Buffer controlled_buffer_1
endmodule

module test_ram (
  input  [2:0] in_1,
  input  [7:0] in_2,
  input  in_3,
  input  in_4,
  input  in_5,
  input  in_6,
  output [7:0] out_7
);

  Ram_principal ram_principal_1 (
    .\Saída_x (out_7), .Seleciona_palavra(in_1), .W(in_5), .Preset(in_3), .Clear(in_4), .Entrada_D(in_2),
    .R(in_6));
endmodule
