// Logisim project 7-Banco de registradores.circ as structural Verilog: 3 circuits, main circuit main
module main (
  input  [7:0] ENTRADA,
  input  CLK,
  output [7:0] SAIDA
);

  and and_1 (SAIDA[0], ENTRADA[0], CLK);
  and and_2 (SAIDA[1], ENTRADA[1], CLK);
  and and_3 (SAIDA[2], ENTRADA[2], CLK);
  and and_4 (SAIDA[3], ENTRADA[3], CLK);
  and and_5 (SAIDA[4], ENTRADA[4], CLK);
  and and_6 (SAIDA[5], ENTRADA[5], CLK);
  and and_7 (SAIDA[6], ENTRADA[6], CLK);
  and and_8 (SAIDA[7], ENTRADA[7], CLK);
endmodule

module Demultiplex (
  input  R,
  input  [2:0] in_2,
  output out_3,
  output out_4,
  output out_5,
  output out_6,
  output out_7,
  output out_8,
  output out_9,
  output out_10
);

  wire and_1_out, and_2_out, and_3_out, and_4_out, and_5_out, and_6_out, and_7_out, and_8_out, not_1_out,
       not_2_out, not_3_out, not_4_out, not_5_out, not_6_out, not_7_out, not_8_out, not_9_out, not_10_out,
       not_11_out, not_12_out;

  not not_1 (not_1_out, in_2[2]);
  not not_2 (not_2_out, in_2[1]);
  not not_3 (not_3_out, in_2[0]);
  not not_4 (not_4_out, in_2[2]);
  not not_5 (not_5_out, in_2[1]);
  not not_6 (not_6_out, in_2[2]);
  not not_7 (not_7_out, in_2[0]);
  not not_8 (not_8_out, in_2[2]);
  not not_9 (not_9_out, in_2[1]);
  not not_10 (not_10_out, in_2[0]);
  not not_11 (not_11_out, in_2[1]);
  not not_12 (not_12_out, in_2[0]);
  and and_1 (and_1_out, not_1_out, not_2_out, not_3_out);
  and and_2 (and_2_out, not_4_out, not_5_out, in_2[0]);
  and and_3 (and_3_out, not_6_out, in_2[1], not_7_out);
  and and_4 (and_4_out, not_8_out, in_2[1], in_2[0]);
  and and_5 (and_5_out, in_2[2], not_9_out, not_10_out);
  and and_6 (and_6_out, in_2[2], not_11_out, in_2[0]);
  and and_7 (and_7_out, in_2[2], in_2[1], not_12_out);
  and and_8 (and_8_out, in_2[2], in_2[1], in_2[0]);
  and and_9 (out_3, R, and_1_out);
  and and_10 (out_4, R, and_2_out);
  and and_11 (out_5, R, and_3_out);
  and and_12 (out_6, R, and_4_out);
  and and_13 (out_7, R, and_5_out);
  and and_14 (out_8, R, and_6_out);
  and and_15 (out_9, R, and_7_out);
  and and_16 (out_10, R, and_8_out);

  // Notes on the sheet:
  //   ENTRADA
endmodule

module Banco (
  input  [7:0] ENTRADA_A,
  input  [2:0] ABC,
  input  in_3,
  output [7:0] SAIDA_A1,
  output [7:0] SAIDA_A2,
  output [7:0] SAIDA_A3,
  output [7:0] SAIDA_A4,
  output [7:0] SAIDA_A5,
  output [7:0] SAIDA_A6,
  output [7:0] SAIDA_A7,
  output [7:0] SAIDA_A8
);

  wire demultiplex_1_out_3, demultiplex_1_out_4, demultiplex_1_out_5, demultiplex_1_out_6,
       demultiplex_1_out_7, demultiplex_1_out_8, demultiplex_1_out_9, demultiplex_1_out_10;

  Demultiplex demultiplex_1 (
    .out_3(demultiplex_1_out_3), .out_4(demultiplex_1_out_4), .out_5(demultiplex_1_out_5),
    .out_6(demultiplex_1_out_6), .out_7(demultiplex_1_out_7), .out_8(demultiplex_1_out_8),
    .out_9(demultiplex_1_out_9), .out_10(demultiplex_1_out_10), .R(in_3), .in_2(ABC));
  main main_1 (.ENTRADA(ENTRADA_A), .CLK(demultiplex_1_out_3), .SAIDA(SAIDA_A1));
  main main_2 (.ENTRADA(ENTRADA_A), .CLK(demultiplex_1_out_4), .SAIDA(SAIDA_A2));
  main main_3 (.ENTRADA(ENTRADA_A), .CLK(demultiplex_1_out_5), .SAIDA(SAIDA_A3));
  main main_4 (.ENTRADA(ENTRADA_A), .CLK(demultiplex_1_out_6), .SAIDA(SAIDA_A4));
  main main_5 (.ENTRADA(ENTRADA_A), .CLK(demultiplex_1_out_7), .SAIDA(SAIDA_A5));
  main main_6 (.ENTRADA(ENTRADA_A), .CLK(demultiplex_1_out_8), .SAIDA(SAIDA_A6));
  main main_7 (.ENTRADA(ENTRADA_A), .CLK(demultiplex_1_out_9), .SAIDA(SAIDA_A7));
  main main_8 (.ENTRADA(ENTRADA_A), .CLK(demultiplex_1_out_10), .SAIDA(SAIDA_A8));
endmodule
