// Logisim project 9-Detector101.circ as structural Verilog: 1 circuit, main circuit main
module main (
  input  [7:0] Entrada,
  input  Clock,
  output \Saída 
);

  wire and_1_out, and_2_out, and_3_out, and_4_out, and_5_out, and_6_out, not_1_out, not_2_out, not_3_out,
       not_4_out, not_5_out, not_6_out;
  wire [7:0] main_1_saida;

  _7_Banco_de_registradores_main main_1 (.ENTRADA(Entrada), .CLK(Clock), .SAIDA(main_1_saida));
  not not_1 (not_1_out, main_1_saida[1]);
  not not_2 (not_2_out, main_1_saida[2]);
  not not_3 (not_3_out, main_1_saida[3]);
  not not_4 (not_4_out, main_1_saida[4]);
  not not_5 (not_5_out, main_1_saida[5]);
  not not_6 (not_6_out, main_1_saida[6]);
  and and_1 (and_1_out, main_1_saida[0], not_1_out, main_1_saida[2]);
  and and_2 (and_2_out, main_1_saida[1], not_2_out, main_1_saida[3]);
  and and_3 (and_3_out, main_1_saida[2], not_3_out, main_1_saida[4]);
  and and_4 (and_4_out, main_1_saida[3], not_4_out, main_1_saida[5]);
  and and_5 (and_5_out, main_1_saida[4], not_5_out, main_1_saida[6]);
  and and_6 (and_6_out, main_1_saida[5], not_6_out, main_1_saida[7]);
  or or_1 (\Saída , and_1_out, and_2_out, and_3_out, and_4_out, and_5_out, and_6_out);

  // Notes on the sheet:
  //   Detector 101 
endmodule
